# Fritzing sketch main (saved by Fritzing 0.9.6b)
breadboards: 1

parts:
  U1 = 7-SEGMENT-DISPLAY [package=7-segment-display]
  PIC_16F877A1 = PIC 16F877A [package=THT]
  R1 = Resistor [tolerance=±5% power=0.25 resistance=220 package=THT]
  R2 = Resistor [tolerance=±5% power=0.25 resistance=220 package=THT]
  R3 = Resistor [tolerance=±5% power=0.25 resistance=220 package=THT]
  R4 = Resistor [tolerance=±5% power=0.25 resistance=220 package=THT]
  R5 = Resistor [tolerance=±5% power=0.25 resistance=220 package=THT]
  R6 = Resistor [tolerance=±5% power=0.25 resistance=220 package=THT]
  R7 = Resistor [tolerance=±5% power=0.25 resistance=220 package=THT]
  S1 = Pushbutton [package="[THT]"]
  S2 = Pushbutton [package="[THT]"]
  R8 = Resistor [tolerance=±5% power=0.25 resistance=1k package=THT]
  R9 = Resistor [tolerance=±5% power=0.25 resistance=1k package=THT]
  C1 = Ceramic Capacitor [capacitance=100nF voltage=35V package="100 mil [THT, multilayer]"]
  C2 = Ceramic Capacitor [capacitance=100nF voltage=35V package="100 mil [THT, multilayer]"]

nets:
  N1: U1.E, R7.Pin_1
  N2: U1.D, R5.Pin_1
  N3: U1.G1, R4.Pin_1
  N4: U1.C, PIC_16F877A1.VSS#30, R8.Pin_1, R9.Pin_1, C1.1, C2.1
  N5: U1.DP, R3.Pin_1
  N6: U1.A, R2.Pin_1
  N7: U1.G2, R1.Pin_1
  N8: U1.G, R6.Pin_1
  N9: PIC_16F877A1.RA0/AN0, PIC_16F877A1.RA1/AN1, PIC_16F877A1.VDD#31, S1.Pin_1, S1.Pin_2, S1.Pin_3, S1.Pin_4, S2.Pin_1, S2.Pin_2, S2.Pin_3, S2.Pin_4, R8.Pin_0, R9.Pin_0, C1.0, C2.0
  N10: PIC_16F877A1.RB1, R7.Pin_0
  N11: PIC_16F877A1.RB2, R6.Pin_0
  N12: PIC_16F877A1.RB3, R5.Pin_0
  N13: PIC_16F877A1.RB4, R4.Pin_0
  N14: PIC_16F877A1.RB5, R3.Pin_0
  N15: PIC_16F877A1.RB6, R2.Pin_0
  N16: PIC_16F877A1.RB7, R1.Pin_0
